// Logisim project Datapath.circ as structural Verilog
module Control (
  input  Op5,
  input  Op4,
  input  Op3,
  input  Op2,
  input  Op1,
  input  Op0,
  output RegDst,
  output ALUSrc,
  output MemtoReg,
  output lRegWrite,
  output MemRead,
  output MemWrite,
  output Branch,
  output [1:0] ALUOp
);

  and and_1 (ALUOp[1], ~Op5, ~Op4, ~Op3, ~Op2, ~Op1, ~Op0);  // AND_Gate
  and and_2 (MemRead, Op5, ~Op4, ~Op3, ~Op2, Op1, Op0);  // AND_Gate
  and and_3 (MemWrite, Op5, ~Op4, Op3, ~Op2, Op1, Op0);  // AND_Gate
  and and_4 (ALUOp[0], ~Op5, ~Op4, ~Op3, Op2, ~Op1, ~Op0);  // AND_Gate
  or or_1 (ALUSrc, MemRead, MemWrite);
  or or_2 (lRegWrite, ALUOp[1], MemRead);

  assign Branch = ALUOp[0];
  assign MemtoReg = MemRead;
  assign RegDst = ALUOp[1];
endmodule
